// Logisim project mesm_6.circ as structural Verilog: 12 circuits, main circuit main
module main (
);

  wire clk, counter_1_carry, cpu_1_dbus_read, cpu_1_dbus_write, cpu_1_ibus_fetch, dram_1_dbus_done,
       irom_1_o_done, IRQ_out, not_1_out, RESET_out;
  wire [1:0] cpu_1_debug_bus;
  wire [14:0] cpu_1_dbus_addr, cpu_1_ibus_addr;
  wire [23:0] cpu_1_dbus_odata_h, cpu_1_dbus_odata_l, dram_1_dbus_odata_h, dram_1_dbus_odata_l,
       irom_1_odata_h, irom_1_odata_l;
  wire [29:0] cycle_counter_cnt;

  Button RESET (.out(RESET_out));
  Button IRQ (.out(IRQ_out));
  Clock u_clk (.out(clk));
  // Probe on cpu_1_ibus_addr
  Counter #(.width(2), .max('h3), .ongoal("stay")) counter_1 (
    .clr(RESET_out), .up(1'b1), .count(1'b1), .clk(clk), .carry(counter_1_carry));  // open: load, D, Q
  IROM irom_1 (
    .CLK(clk), .FETCH(cpu_1_ibus_fetch), .I_ADDR(cpu_1_ibus_addr), .ODATA_L(irom_1_odata_l),
    .ODATA_H(irom_1_odata_h), .O_DONE(irom_1_o_done));
  // Probe on irom_1_odata_l
  // Probe on irom_1_odata_h
  not not_1 (not_1_out, counter_1_carry);
  CPU cpu_1 (
    .CLK(clk), .RESET(not_1_out), .INTRPT(IRQ_out), .IBUS_IDATA_L(irom_1_odata_l),
    .IBUS_IDATA_H(irom_1_odata_h), .IBUS_DONE(irom_1_o_done), .DBUS_IDATA_L(dram_1_dbus_odata_l),
    .DBUS_IDATA_H(dram_1_dbus_odata_h), .DBUS_DONE(dram_1_dbus_done), .IBUS_FETCH(cpu_1_ibus_fetch),
    .IBUS_ADDR(cpu_1_ibus_addr), .DBUS_READ(cpu_1_dbus_read), .DBUS_WRITE(cpu_1_dbus_write),
    .DBUS_ADDR(cpu_1_dbus_addr), .DBUS_ODATA_L(cpu_1_dbus_odata_l), .DBUS_ODATA_H(cpu_1_dbus_odata_h),
    .DEBUG_BUS(cpu_1_debug_bus));
  // NOR_Gate nor_1 has open pins: in0=cpu_1_debug_bus[0], in1=cpu_1_debug_bus[1], out=open
  // Probe on cpu_1_dbus_addr
  // Probe on cpu_1_dbus_odata_l
  // Probe on cpu_1_dbus_odata_h
  LED TestFail (.in(cpu_1_debug_bus[0]));
  LED TestPass (.in(cpu_1_debug_bus[1]));
  // Probe on cycle_counter_cnt
  CYC_CNT cycle_counter (.CLK(clk), .EN(1'b1), .CNT(cycle_counter_cnt));
  // Probe on dram_1_dbus_odata_l
  // Probe on dram_1_dbus_odata_h
  DRAM dram_1 (
    .CLK(clk), .DBUS_READ(cpu_1_dbus_read), .DBUS_WRITE(cpu_1_dbus_write), .DBUS_ADDR(cpu_1_dbus_addr),
    .DBUS_IDATA_L(cpu_1_dbus_odata_l), .DBUS_IDATA_H(cpu_1_dbus_odata_h), .DBUS_DONE(dram_1_dbus_done),
    .DBUS_ODATA_L(dram_1_dbus_odata_l), .DBUS_ODATA_H(dram_1_dbus_odata_h));

  // Notes on the sheet:
  //   POWERON_RESET
endmodule

module M_regs (
  input  clk,
  input  [1:0] sel_mr,
  input  [3:0] reg_index,
  input  [8:0] imm,
  input  [14:0] Vaddr,
  input  [14:0] Uaddr,
  input  [1:0] sel_mw,
  input  w_m,
  input  [2:0] sel_md,
  input  [15:0] PC,
  input  [23:0] ACC_L,
  input  [14:0] Mr_q,
  output [14:0] Mi,
  output [14:0] Mr,
  output Mi_z
);

  wire decoder_1_out1, decoder_1_out2, decoder_1_out3, decoder_1_out4, decoder_1_out5, decoder_1_out6,
       decoder_1_out7, decoder_1_out8, decoder_1_out9, decoder_1_out10, decoder_1_out11, decoder_1_out12,
       decoder_1_out13, decoder_1_out14, decoder_1_out15, decoder_2_out0, decoder_2_out1, decoder_2_out2,
       decoder_2_out3, decoder_2_out4, decoder_2_out5, decoder_2_out6, decoder_2_out7, decoder_2_out8,
       decoder_2_out9, decoder_2_out10, decoder_2_out11, decoder_2_out12, decoder_2_out13, decoder_2_out14,
       decoder_2_out15, decoder_3_out0, decoder_3_out1, decoder_3_out2, decoder_3_out3, decoder_3_out4,
       decoder_3_out5, decoder_3_out6, decoder_3_out7, decoder_3_out8, decoder_3_out9, decoder_3_out10,
       decoder_3_out11, decoder_3_out12, decoder_3_out13, decoder_3_out14, decoder_3_out15;
  wire [3:0] bit_extender_1_out, bit_extender_2_out, bit_extender_3_out, bit_extender_4_out,
       bit_extender_5_out, bit_extender_6_out, m_ra, m_wa;
  wire [14:0] adder_1_out, bit_extender_7_out, M1_q, M2_q, M3_q, M4_q, M5_q, M6_q, M7_q, M8_q, M9_q, M10_q,
       M11_q, M12_q, M13_q, M14_q, M15_q, multiplexer_3_out, subtractor_1_out;

  Bit_Extender #(.in_width(9), .out_width(4), .\type ("zero")) bit_extender_1 (.in(imm), .out(bit_extender_1_out));
  Bit_Extender #(.in_width(15), .out_width(4), .\type ("zero")) bit_extender_2 (.in(Vaddr), .out(bit_extender_2_out));
  Bit_Extender #(.in_width(15), .out_width(4), .\type ("zero")) bit_extender_3 (.in(Uaddr), .out(bit_extender_3_out));
  Bit_Extender #(.in_width(9), .out_width(4), .\type ("zero")) bit_extender_4 (.in(imm), .out(bit_extender_4_out));
  Bit_Extender #(.in_width(15), .out_width(4), .\type ("zero")) bit_extender_5 (.in(Vaddr), .out(bit_extender_5_out));
  Bit_Extender #(.in_width(15), .out_width(4), .\type ("zero")) bit_extender_6 (.in(Uaddr), .out(bit_extender_6_out));
  Bit_Extender #(.in_width(24), .out_width(15), .\type ("zero")) bit_extender_7 (.in(ACC_L), .out(bit_extender_7_out));
  Adder #(.width(15)) adder_1 (.a(Mr_q), .b(15'h1), .out(adder_1_out));  // open: cin, cout
  Subtractor #(.width(15)) subtractor_1 (.a(Mr_q), .b(15'h1), .out(subtractor_1_out));  // open: bin, bout
  Multiplexer #(.select(2), .width(4), .enable("false")) multiplexer_1 (
    .in0(reg_index), .in1(bit_extender_4_out), .in2(bit_extender_5_out), .in3(bit_extender_6_out),
    .out(m_ra), .sel(sel_mr));
  Multiplexer #(.select(2), .width(4), .enable("false")) multiplexer_2 (
    .in0(reg_index), .in1(bit_extender_1_out), .in2(bit_extender_2_out), .in3(bit_extender_3_out),
    .out(m_wa), .sel(sel_mw));
  Multiplexer #(.select(3), .width(15), .enable("false")) multiplexer_3 (
    .in0(PC[15:1]), .in1(bit_extender_7_out), .in2(Mr_q), .in3(adder_1_out), .in4(subtractor_1_out),
    .in5(Vaddr), .in6(Uaddr), .out(multiplexer_3_out), .sel(sel_md));  // open: in7
  Decoder #(.select(4)) decoder_1 (
    .out1(decoder_1_out1), .out2(decoder_1_out2), .out3(decoder_1_out3), .out4(decoder_1_out4),
    .out5(decoder_1_out5), .out6(decoder_1_out6), .out7(decoder_1_out7), .out8(decoder_1_out8),
    .out9(decoder_1_out9), .out10(decoder_1_out10), .out11(decoder_1_out11), .out12(decoder_1_out12),
    .out13(decoder_1_out13), .out14(decoder_1_out14), .out15(decoder_1_out15), .sel(m_wa), .en(w_m));  // open: out0
  Register #(.width(15)) M1 (.D(multiplexer_3_out), .en(decoder_1_out1), .clk(clk), .Q(M1_q), .clr(1'b0));
  Register #(.width(15)) M2 (.D(multiplexer_3_out), .en(decoder_1_out2), .clk(clk), .Q(M2_q), .clr(1'b0));
  Register #(.width(15)) M3 (.D(multiplexer_3_out), .en(decoder_1_out3), .clk(clk), .Q(M3_q), .clr(1'b0));
  Register #(.width(15)) M4 (.D(multiplexer_3_out), .en(decoder_1_out4), .clk(clk), .Q(M4_q), .clr(1'b0));
  assign Mi = decoder_3_out1 ? M1_q : 15'bz;  // Controlled_Buffer controlled_buffer_1
  assign Mr = decoder_2_out1 ? M1_q : 15'bz;  // Controlled_Buffer controlled_buffer_2
  assign Mi = decoder_3_out2 ? M2_q : 15'bz;  // Controlled_Buffer controlled_buffer_3
  assign Mr = decoder_2_out2 ? M2_q : 15'bz;  // Controlled_Buffer controlled_buffer_4
  assign Mi = decoder_3_out3 ? M3_q : 15'bz;  // Controlled_Buffer controlled_buffer_5
  assign Mr = decoder_2_out3 ? M3_q : 15'bz;  // Controlled_Buffer controlled_buffer_6
  assign Mi = decoder_3_out4 ? M4_q : 15'bz;  // Controlled_Buffer controlled_buffer_7
  assign Mr = decoder_2_out4 ? M4_q : 15'bz;  // Controlled_Buffer controlled_buffer_8
  Decoder #(.select(4), .enable("false")) decoder_2 (
    .out0(decoder_2_out0), .out1(decoder_2_out1), .out2(decoder_2_out2), .out3(decoder_2_out3),
    .out4(decoder_2_out4), .out5(decoder_2_out5), .out6(decoder_2_out6), .out7(decoder_2_out7),
    .out8(decoder_2_out8), .out9(decoder_2_out9), .out10(decoder_2_out10), .out11(decoder_2_out11),
    .out12(decoder_2_out12), .out13(decoder_2_out13), .out14(decoder_2_out14), .out15(decoder_2_out15),
    .sel(m_ra));
  Decoder #(.select(4), .enable("false")) decoder_3 (
    .out0(decoder_3_out0), .out1(decoder_3_out1), .out2(decoder_3_out2), .out3(decoder_3_out3),
    .out4(decoder_3_out4), .out5(decoder_3_out5), .out6(decoder_3_out6), .out7(decoder_3_out7),
    .out8(decoder_3_out8), .out9(decoder_3_out9), .out10(decoder_3_out10), .out11(decoder_3_out11),
    .out12(decoder_3_out12), .out13(decoder_3_out13), .out14(decoder_3_out14), .out15(decoder_3_out15),
    .sel(reg_index));
  Register #(.width(15)) M5 (.D(multiplexer_3_out), .en(decoder_1_out5), .clk(clk), .Q(M5_q), .clr(1'b0));
  Register #(.width(15)) M6 (.D(multiplexer_3_out), .en(decoder_1_out6), .clk(clk), .Q(M6_q), .clr(1'b0));
  Register #(.width(15)) M7 (.D(multiplexer_3_out), .en(decoder_1_out7), .clk(clk), .Q(M7_q), .clr(1'b0));
  Register #(.width(15)) M8 (.D(multiplexer_3_out), .en(decoder_1_out8), .clk(clk), .Q(M8_q), .clr(1'b0));
  assign Mi = decoder_3_out5 ? M5_q : 15'bz;  // Controlled_Buffer controlled_buffer_9
  assign Mr = decoder_2_out5 ? M5_q : 15'bz;  // Controlled_Buffer controlled_buffer_10
  assign Mi = decoder_3_out6 ? M6_q : 15'bz;  // Controlled_Buffer controlled_buffer_11
  assign Mr = decoder_2_out6 ? M6_q : 15'bz;  // Controlled_Buffer controlled_buffer_12
  assign Mi = decoder_3_out7 ? M7_q : 15'bz;  // Controlled_Buffer controlled_buffer_13
  assign Mr = decoder_2_out7 ? M7_q : 15'bz;  // Controlled_Buffer controlled_buffer_14
  assign Mi = decoder_3_out8 ? M8_q : 15'bz;  // Controlled_Buffer controlled_buffer_15
  assign Mr = decoder_2_out8 ? M8_q : 15'bz;  // Controlled_Buffer controlled_buffer_16
  Register #(.width(15)) M9 (.D(multiplexer_3_out), .en(decoder_1_out9), .clk(clk), .Q(M9_q), .clr(1'b0));
  Register #(.width(15)) M10 (.D(multiplexer_3_out), .en(decoder_1_out10), .clk(clk), .Q(M10_q), .clr(1'b0));
  Register #(.width(15)) M11 (.D(multiplexer_3_out), .en(decoder_1_out11), .clk(clk), .Q(M11_q), .clr(1'b0));
  Register #(.width(15)) M12 (.D(multiplexer_3_out), .en(decoder_1_out12), .clk(clk), .Q(M12_q), .clr(1'b0));
  assign Mi = decoder_3_out9 ? M9_q : 15'bz;  // Controlled_Buffer controlled_buffer_17
  assign Mr = decoder_2_out9 ? M9_q : 15'bz;  // Controlled_Buffer controlled_buffer_18
  assign Mi = decoder_3_out10 ? M10_q : 15'bz;  // Controlled_Buffer controlled_buffer_19
  assign Mr = decoder_2_out10 ? M10_q : 15'bz;  // Controlled_Buffer controlled_buffer_20
  assign Mi = decoder_3_out11 ? M11_q : 15'bz;  // Controlled_Buffer controlled_buffer_21
  assign Mr = decoder_2_out11 ? M11_q : 15'bz;  // Controlled_Buffer controlled_buffer_22
  assign Mi = decoder_3_out12 ? M12_q : 15'bz;  // Controlled_Buffer controlled_buffer_23
  assign Mr = decoder_2_out12 ? M12_q : 15'bz;  // Controlled_Buffer controlled_buffer_24
  Register #(.width(15)) M13 (.D(multiplexer_3_out), .en(decoder_1_out13), .clk(clk), .Q(M13_q), .clr(1'b0));
  Register #(.width(15)) M14 (.D(multiplexer_3_out), .en(decoder_1_out14), .clk(clk), .Q(M14_q), .clr(1'b0));
  Register #(.width(15)) M15 (.D(multiplexer_3_out), .en(decoder_1_out15), .clk(clk), .Q(M15_q), .clr(1'b0));
  assign Mi = decoder_3_out13 ? M13_q : 15'bz;  // Controlled_Buffer controlled_buffer_25
  assign Mr = decoder_2_out13 ? M13_q : 15'bz;  // Controlled_Buffer controlled_buffer_26
  assign Mi = decoder_3_out14 ? M14_q : 15'bz;  // Controlled_Buffer controlled_buffer_27
  assign Mr = decoder_2_out14 ? M14_q : 15'bz;  // Controlled_Buffer controlled_buffer_28
  assign Mi = decoder_3_out15 ? M15_q : 15'bz;  // Controlled_Buffer controlled_buffer_29
  assign Mr = decoder_2_out15 ? M15_q : 15'bz;  // Controlled_Buffer controlled_buffer_30
  assign Mi = decoder_3_out0 ? {15{1'b0}} : 15'bz;  // Controlled_Buffer controlled_buffer_31
  assign Mr = decoder_2_out0 ? {15{1'b0}} : 15'bz;  // Controlled_Buffer controlled_buffer_32
  Comparator #(.width(15)) comparator_1 (.a(Mi), .b({15{1'b0}}), .eq(Mi_z));  // open: gt, lt

  // Other names for the same wires on the sheet: P_SEL_MW[1:0] = sel_mw

  // Notes on the sheet:
  //   WA
  //   RA1
  //   RA2
endmodule

module ALU (
  input  CLK,
  input  [23:0] ALU_A_H,
  input  [23:0] ALU_A_L,
  input  [23:0] ALU_B_H,
  input  [23:0] ALU_B_L,
  input  [5:0] ALU_OP,
  output [23:0] ALU_R_H,
  output [23:0] ALU_R_L,
  output [23:0] ALU_Y_H,
  output [23:0] ALU_Y_L,
  output ALU_DONE
);


  assign ALU_DONE = 1'b0;
endmodule

module IROM (
  input  CLK,
  input  FETCH,
  input  [14:0] I_ADDR,
  output [23:0] ODATA_L,
  output [23:0] ODATA_H,
  output O_DONE
);

  wire and_1_out, not_1_out;
  wire [23:0] IROM_H_data, IROM_L_data;

  ROM #(.addrWidth(15), .dataWidth(24)) IROM_L (.addr(I_ADDR), .data(IROM_L_data));
  Register #(.width(1)) register_1 (.D(FETCH), .en(1'b1), .clk(CLK), .Q(O_DONE), .clr(1'b0));
  not not_1 (not_1_out, O_DONE);
  and and_1 (and_1_out, FETCH, not_1_out);
  Register #(.width(24)) register_2 (.D(IROM_L_data), .en(and_1_out), .clk(CLK), .Q(ODATA_L), .clr(1'b0));
  ROM #(.addrWidth(15), .dataWidth(24)) IROM_H (.addr(I_ADDR), .data(IROM_H_data));
  Register #(.width(24)) register_3 (.D(IROM_H_data), .en(and_1_out), .clk(CLK), .Q(ODATA_H), .clr(1'b0));

  // Notes on the sheet:
  //   contents of IROM_L (hex, n*v repeats v):
  //   0 90000 90000 90000 32763*0 ffff
  //   contents of IROM_H (hex, n*v repeats v):
  //   0 c0003 2dfd63 6d94e5
endmodule

module CPU (
  input  CLK,
  input  RESET,
  input  INTRPT,
  input  [23:0] IBUS_IDATA_L,
  input  [23:0] IBUS_IDATA_H,
  input  IBUS_DONE,
  input  [23:0] DBUS_IDATA_L,
  input  [23:0] DBUS_IDATA_H,
  input  DBUS_DONE,
  output IBUS_FETCH,
  output [14:0] IBUS_ADDR,
  output DBUS_READ,
  output DBUS_WRITE,
  output [14:0] DBUS_ADDR,
  output [23:0] DBUS_ODATA_L,
  output [23:0] DBUS_ODATA_H,
  output [1:0] DEBUG_BUS
);

  wire ACC_IS_ZERO, alu_done, and_2_out, and_3_out, and_4_out, and_5_out, and_6_out, and_7_out, and_8_out,
       and_9_out, and_12_out, and_13_out, and_14_out, and_16_out, branch, busy, comparator_1_eq,
       comparator_2_eq, comparator_3_eq, comparator_4_eq, comparator_5_eq, comparator_7_eq, comparator_8_eq,
       comparator_9_eq, cond_acc_neg, cond_acc_nonzero, cond_acc_zero, cond_op_not_cached, decode,
       enter_interrupt, exit_interrupt, gie, irq, IS_OP_CACHED, m_w, Mi_is_zero, multiplexer_12_out,
       multiplexer_13_out, nand_1_out, nor_1_out, not_1_out, not_2_out, not_3_out, not_4_out, not_5_out,
       not_6_out, not_7_out, not_8_out, not_9_out, not_10_out, not_11_out, not_12_out, not_13_out,
       not_14_out, not_15_out, not_16_out, not_17_out, not_18_out, op_lflag, op_utc0, op_xta0, or_1_out,
       or_4_out, or_5_out, or_6_out, or_7_out, P_BRANCH, P_C_ACTIVE, P_DECODE, P_ENTER_INT, P_EXIT_INT,
       P_M_NONZERO, P_M_W, P_M_ZERO, P_R_ADD, P_SEL_ADDR, P_SEL_ALU_MEM, P_W_A, P_W_C, P_W_PC, sel_c_mem,
       w_acc, w_c, w_opcode, w_pc;
  wire [0:0] PC_Q;
  wire [1:0] P_SEL_MR, P_SEL_MW;
  wire [2:0] P_SEL_ACC, P_SEL_MD, P_SEL_PC;
  wire [3:0] op_ir, reg_index;
  wire [5:0] alu_op, R_Q;
  wire [8:0] adder_1_out, imm, jmp_tbl_1_mc_addr, multiplexer_3_out, multiplexer_4_out, multiplexer_5_out,
       multiplexer_6_out, multiplexer_9_out, upc_next, UPC_q;
  wire [14:0] adder_3_out, bit_extender_3_out, bit_extender_4_out, C_Q, Mi, Mr, multiplexer_16_out,
       multiplexer_17_out, multiplexer_18_out, op_addr, PC_CACHED_q, Uaddr, Vaddr;
  wire [15:0] multiplexer_7_out, multiplexer_10_out, multiplexer_11_out, pc_plus_1;
  wire [23:0] ALU_R_H, ALU_R_L, bit_extender_1_out, bit_extender_2_out, multiplexer_1_out, multiplexer_2_out,
       opcode, OPCODE_CACHE_H_q, OPCODE_CACHE_L_q, Y_H, Y_L;
  wire [31:0] mc_rom_1_uop_h, mc_rom_1_uop_l;
  wire [31:3] uop_h;

  assign bit_extender_1_out = {{9{1'b0}}, Mr};  // Bit_Extender bit_extender_1
  assign bit_extender_2_out = {{18{1'b0}}, R_Q};  // Bit_Extender bit_extender_2
  or or_1 (or_1_out, DBUS_READ, DBUS_WRITE);
  not not_1 (not_1_out, DBUS_DONE);
  not not_2 (not_2_out, IBUS_DONE);
  Comparator #(.width(6)) comparator_1 (.a(alu_op), .b({6{1'b0}}), .eq(comparator_1_eq));  // open: gt, lt
  not not_3 (not_3_out, alu_done);
  not not_4 (not_4_out, busy);
  and and_1 (decode, not_4_out, P_DECODE);
  and and_2 (and_2_out, cond_op_not_cached, not_5_out);
  not not_5 (not_5_out, IS_OP_CACHED);
  and and_3 (and_3_out, cond_acc_zero, ACC_IS_ZERO);
  not not_6 (not_6_out, ACC_IS_ZERO);
  and and_4 (and_4_out, not_6_out, cond_acc_nonzero);
  and and_5 (and_5_out, cond_acc_neg, DBUS_ODATA_H[8]);
  and and_6 (and_6_out, P_M_ZERO, Mi_is_zero);
  and and_7 (and_7_out, or_1_out, not_1_out);
  and and_8 (and_8_out, IBUS_FETCH, not_2_out);
  not not_7 (not_7_out, comparator_1_eq);
  and and_9 (and_9_out, not_7_out, not_3_out);
  or or_2 (busy, and_7_out, and_8_out, and_9_out);
  or or_3 (branch, and_2_out, and_3_out, and_4_out, and_5_out, and_6_out, P_BRANCH);
  Register #(.width(6)) R (.Q(R_Q));  // open: D, en, clk, clr
  not not_8 (not_8_out, busy);
  Multiplexer #(.select(3), .width(24)) multiplexer_1 (
    .in0(DBUS_IDATA_L), .in1(bit_extender_1_out), .in2(bit_extender_2_out), .in3(Y_L), .in4(ALU_R_L),
    .out(multiplexer_1_out), .sel(P_SEL_ACC), .en(nand_1_out));  // open: in5, in6, in7
  Multiplexer #(.select(3), .width(24)) multiplexer_2 (
    .in0(DBUS_IDATA_H), .in1({24{1'b0}}), .in2({24{1'b0}}), .in3(Y_H), .in4(ALU_R_H),
    .out(multiplexer_2_out), .sel(P_SEL_ACC), .en(nand_1_out));  // open: in5, in6, in7
  not not_9 (not_9_out, w_acc);
  and and_10 (w_acc, not_8_out, P_W_A);
  nand nand_1 (nand_1_out, not_9_out, op_xta0);
  REG_48 Y (.Q_L(Y_L), .Q_H(Y_H));  // open: CLK, WE, D_L, D_H
  or or_4 (or_4_out, op_xta0, op_utc0);
  JMP_TBL jmp_tbl_1 (.CMD(opcode), .MC_ADDR(jmp_tbl_1_mc_addr));
  Multiplexer #(.width(9), .enable("false")) multiplexer_3 (
    .in0(jmp_tbl_1_mc_addr), .in1(9'h16), .out(multiplexer_3_out), .sel(or_4_out));
  REG_48 ACC (
    .CLK(CLK), .WE(w_acc), .D_L(multiplexer_1_out), .D_H(multiplexer_2_out), .Q_L(DBUS_ODATA_L),
    .Q_H(DBUS_ODATA_H));
  Comparator #(.width(24)) comparator_2 (.a(DBUS_ODATA_L), .b({24{1'b0}}), .eq(comparator_2_eq));  // open: gt, lt
  Comparator #(.width(24)) comparator_3 (.a(DBUS_ODATA_H), .b({24{1'b0}}), .eq(comparator_3_eq));  // open: gt, lt
  Multiplexer #(.width(9), .enable("false")) multiplexer_4 (
    .in0(multiplexer_3_out), .in1(9'h17), .out(multiplexer_4_out), .sel(irq));
  assign bit_extender_3_out = {{6{imm[8]}}, imm};  // Bit_Extender bit_extender_3
  and and_11 (ACC_IS_ZERO, comparator_2_eq, comparator_3_eq);
  ALU alu_1 (
    .CLK(CLK), .ALU_OP(alu_op), .ALU_DONE(alu_done));  // open: ALU_A_H, ALU_A_L, ALU_B_H, ALU_B_L, ALU_R_H, ALU_R_L, ALU_Y_H, ALU_Y_L
  Adder #(.width(9)) adder_1 (.a(9'h1), .b(UPC_q), .out(adder_1_out));  // open: cin, cout
  Multiplexer #(.width(9), .enable("false")) multiplexer_5 (
    .in0(adder_1_out), .in1(multiplexer_4_out), .out(multiplexer_5_out), .sel(decode));
  Multiplexer #(.width(9), .enable("false")) multiplexer_6 (
    .in0(multiplexer_5_out), .in1(imm), .out(multiplexer_6_out), .sel(branch));
  // Probe on P_SEL_PC
  Multiplexer #(.select(3), .width(16), .enable("false")) multiplexer_7 (
    .in0({Uaddr, 1'b0}), .in1({Vaddr, 1'b0}), .in2({Mi, 1'b0}), .in3({bit_extender_3_out, 1'b0}),
    .in4(pc_plus_1), .out(multiplexer_7_out), .sel(P_SEL_PC));  // open: in5, in6, in7
  Comparator #(.width(24)) comparator_4 (.a(opcode), .b(24'h6d94e5), .eq(comparator_4_eq));  // open: gt, lt
  Comparator #(.width(24)) comparator_5 (.a(opcode), .b(24'h2dfd63), .eq(comparator_5_eq));  // open: gt, lt
  Multiplexer #(.width(15), .enable("false")) multiplexer_8 (.in0(Uaddr), .in1(Mr), .out(DBUS_ADDR), .sel(P_SEL_ADDR));
  Multiplexer #(.width(9), .enable("false")) multiplexer_9 (
    .in0(multiplexer_6_out), .in1(UPC_q), .out(multiplexer_9_out), .sel(busy));
  not not_10 (not_10_out, busy);
  and and_12 (and_12_out, decode, IS_OP_CACHED);
  // Probe on IBUS_IDATA_L
  // Probe on IBUS_IDATA_H
  and and_13 (and_13_out, P_DECODE, comparator_4_eq);
  and and_14 (and_14_out, P_DECODE, comparator_5_eq);
  // Probe on upc_next
  // Probe on multiplexer_10_out
  and and_15 (w_pc, not_10_out, P_W_PC);
  Multiplexer #(.width(16), .enable("false")) multiplexer_10 (
    .in0(multiplexer_11_out), .in1(multiplexer_7_out), .out(multiplexer_10_out), .sel(w_pc));
  Multiplexer #(.width(16), .enable("false")) multiplexer_11 (
    .in0({IBUS_ADDR, PC_Q[0]}), .in1(pc_plus_1), .out(multiplexer_11_out), .sel(and_12_out));
  Register #(.width(1), .trigger("falling")) register_1 (
    .D(and_13_out), .en(nor_1_out), .clk(CLK), .Q(DEBUG_BUS[1]), .clr(RESET));
  Register #(.width(1), .trigger("falling")) register_2 (
    .D(and_14_out), .en(nor_1_out), .clk(CLK), .Q(DEBUG_BUS[0]), .clr(RESET));
  and and_16 (and_16_out, INTRPT, gie);
  Multiplexer #(.enable("false")) multiplexer_12 (.in0(and_16_out), .in1(1'b0), .out(multiplexer_12_out), .sel(RESET));
  not not_11 (not_11_out, busy);
  not not_12 (not_12_out, busy);
  or or_5 (or_5_out, enter_interrupt, RESET);
  Multiplexer #(.enable("false")) multiplexer_13 (
    .in0(exit_interrupt), .in1(1'b0), .out(multiplexer_13_out), .sel(or_5_out));
  Multiplexer #(.width(9), .enable("false")) multiplexer_14 (
    .in0(multiplexer_9_out), .in1({9{1'b1}}), .out(upc_next), .sel(RESET));
  Register #(.width(16)) PC (.D(multiplexer_10_out), .en(1'b1), .clk(CLK), .Q({IBUS_ADDR, PC_Q[0]}), .clr(1'b0));
  Register #(.width(24)) OPCODE_CACHE_L (
    .D(IBUS_IDATA_L), .en(w_opcode), .clk(CLK), .Q(OPCODE_CACHE_L_q));  // open: clr
  Register #(.width(24)) OPCODE_CACHE_H (
    .D(IBUS_IDATA_H), .en(w_opcode), .clk(CLK), .Q(OPCODE_CACHE_H_q));  // open: clr
  Register #(.width(15)) PC_CACHED (.D(IBUS_ADDR), .en(w_opcode), .clk(CLK), .Q(PC_CACHED_q));  // open: clr
  nor nor_1 (nor_1_out, DEBUG_BUS[1], DEBUG_BUS[0]);
  Register #(.width(1)) u_irq (.D(multiplexer_12_out), .en(1'b1), .clk(CLK), .Q(irq), .clr(1'b0));
  and and_17 (exit_interrupt, not_11_out, P_EXIT_INT);
  and and_18 (enter_interrupt, not_12_out, P_ENTER_INT);
  or or_6 (or_6_out, exit_interrupt, or_5_out);
  Register #(.width(1)) u_gie (.D(multiplexer_13_out), .en(or_6_out), .clk(CLK), .Q(gie), .clr(1'b0));
  Register #(.width(9)) UPC (.D(upc_next), .en(1'b1), .clk(CLK), .Q(UPC_q), .clr(1'b0));
  Adder #(.width(16)) adder_2 (.a(16'h1), .b({IBUS_ADDR, PC_Q[0]}), .out(pc_plus_1));  // open: cin, cout
  Comparator #(.width(15)) comparator_6 (.a(PC_CACHED_q), .b(IBUS_ADDR), .eq(IS_OP_CACHED));  // open: gt, lt
  not not_13 (not_13_out, busy);
  and and_19 (m_w, not_13_out, P_M_W);
  // Probe on mc_rom_1_uop_l
  // Probe on mc_rom_1_uop_h
  not not_14 (not_14_out, RESET);
  MC_ROM mc_rom_1 (.ADDR(upc_next), .UOP_L(mc_rom_1_uop_l), .UOP_H(mc_rom_1_uop_h));
  Multiplexer #(.width(24), .enable("false")) multiplexer_15 (
    .in0(OPCODE_CACHE_H_q), .in1(OPCODE_CACHE_L_q), .out(opcode), .sel(PC_Q[0]));
  // Probe on opcode
  Register #(.width(32)) uop_l (
    .D(mc_rom_1_uop_l), .en(not_14_out), .clk(CLK),
    .Q({P_R_ADD, P_SEL_ADDR, P_SEL_PC, P_M_NONZERO, P_SEL_MR, P_M_W, P_SEL_MW, P_SEL_MD, P_SEL_ACC, alu_op, imm}),
    .clr(RESET));
  Register #(.width(32)) u_uop_h (
    .D(mc_rom_1_uop_h), .en(not_14_out), .clk(CLK),
    .Q({uop_h[31:19], P_SEL_ALU_MEM, P_M_ZERO, P_W_PC, P_EXIT_INT, P_ENTER_INT, P_C_ACTIVE, P_BRANCH, cond_acc_zero, cond_acc_neg, cond_acc_nonzero, P_W_C, P_W_A, DBUS_WRITE, DBUS_READ, P_DECODE, uop_h[3], IBUS_FETCH, cond_op_not_cached, sel_c_mem}),
    .clr(RESET));
  // Probe on IBUS_ADDR
  M_regs m_regs_1 (
    .clk(CLK), .sel_mr(P_SEL_MR), .reg_index(reg_index), .imm(imm), .Vaddr(Vaddr), .Uaddr(Uaddr),
    .sel_mw(P_SEL_MW), .w_m(m_w), .sel_md(P_SEL_MD), .PC({IBUS_ADDR, PC_Q[0]}), .ACC_L(DBUS_ODATA_L),
    .Mr_q(Mr), .Mi(Mi), .Mr(Mr), .Mi_z(Mi_is_zero));
  // Probe on imm
  Comparator #(.width(24)) comparator_7 (.a(opcode), .b(24'h22000), .eq(comparator_7_eq));  // open: gt, lt
  Comparator #(.width(24)) comparator_8 (.a(opcode), .b(24'h8000), .eq(comparator_8_eq));  // open: gt, lt
  Comparator #(.width(24)) comparator_9 (.a(opcode), .b(24'h90000), .eq(comparator_9_eq));  // open: gt, lt
  OP_SPLITTER op_splitter_1 (
    .OPCODE(opcode), .OP_LFLAG(op_lflag), .OP_IR(op_ir), .OP_ADDR(op_addr));  // open: OP_LCMD, OP_SCMD
  not not_15 (not_15_out, P_C_ACTIVE);
  or or_7 (or_7_out, comparator_7_eq, comparator_8_eq);
  not not_16 (not_16_out, P_C_ACTIVE);
  and and_20 (op_xta0, not_15_out, or_7_out);
  and and_21 (op_utc0, not_16_out, comparator_9_eq);
  Adder #(.width(15)) adder_3 (.a(op_addr), .b(C_Q), .out(adder_3_out));  // open: cin, cout
  Multiplexer #(.width(15), .enable("false")) multiplexer_16 (
    .in0(Vaddr), .in1(Mr), .out(multiplexer_16_out), .sel(P_R_ADD));
  not not_17 (not_17_out, busy);
  Bit_Extender #(.in_width(24), .out_width(15), .\type ("zero")) bit_extender_4 (
    .in(DBUS_IDATA_L), .out(bit_extender_4_out));
  Multiplexer #(.width(15), .enable("false")) multiplexer_17 (
    .in0(op_addr), .in1(adder_3_out), .out(multiplexer_17_out), .sel(P_C_ACTIVE));
  Adder #(.width(15)) adder_4 (.a(multiplexer_16_out), .b(Mi), .out(Uaddr));  // open: cin, cout
  and and_22 (w_c, not_17_out, P_W_C);
  Multiplexer #(.width(15), .enable("false")) multiplexer_18 (
    .in0(Uaddr), .in1(bit_extender_4_out), .out(multiplexer_18_out), .sel(sel_c_mem));
  not not_18 (not_18_out, busy);
  Register #(.width(15)) C (.D(multiplexer_18_out), .en(w_c), .clk(CLK), .Q(C_Q), .clr(1'b0));
  Register #(.width(15)) u_Vaddr (.D(multiplexer_17_out), .en(decode), .clk(CLK), .Q(Vaddr), .clr(1'b0));
  Register #(.width(4)) u_reg_index (.D(op_ir), .en(decode), .clk(CLK), .Q(reg_index), .clr(1'b0));
  and and_23 (w_opcode, not_18_out, uop_h[3]);

  // Other names for the same wires on the sheet: ACC_H[23:0] = DBUS_ODATA_H; ACC_IS_NEG = DBUS_ODATA_H[8];
  //   ACC_L[23:0] = DBUS_ODATA_L; test_fail = DEBUG_BUS[0]; test_pass = DEBUG_BUS[1]; interrupt = INTRPT;
  //   PC_Q[15:1] = IBUS_ADDR;
  //   uop_h (some bits) = {P_SEL_ALU_MEM, P_M_ZERO, P_W_PC, P_EXIT_INT, P_ENTER_INT, P_C_ACTIVE, P_BRANCH, cond_acc_zero, cond_acc_neg, cond_acc_nonzero, P_W_C, P_W_A, DBUS_WRITE, DBUS_READ, P_DECODE, IBUS_FETCH, cond_op_not_cached, sel_c_mem};
  //   P_OP_NOTCACHED = cond_op_not_cached; fetch = IBUS_FETCH; mem_r = DBUS_READ; mem_w = DBUS_WRITE;
  //   P_A_NONZERO = cond_acc_nonzero; P_A_ZERO = cond_acc_zero; uncond_branch = P_BRANCH;
  //   uop_l[31:0] = {P_R_ADD, P_SEL_ADDR, P_SEL_PC, P_M_NONZERO, P_SEL_MR, P_M_W, P_SEL_MW, P_SEL_MD, P_SEL_ACC, alu_op, imm}

  // Notes on the sheet:
  //   TODO
  //   optimization for XTA 0
endmodule

module DRAM (
  input  CLK,
  input  DBUS_READ,
  input  DBUS_WRITE,
  input  [14:0] DBUS_ADDR,
  input  [23:0] DBUS_IDATA_L,
  input  [23:0] DBUS_IDATA_H,
  output DBUS_DONE,
  output [23:0] DBUS_ODATA_L,
  output [23:0] DBUS_ODATA_H
);

  wire comparator_1_eq, comparator_2_eq, or_1_out;
  wire [23:0] multiplexer_1_out, multiplexer_2_out, ram_1_dout, ram_2_dout;

  RAM #(.addrWidth(15), .dataWidth(24), .databus("bibus")) ram_1 (
    .addr(DBUS_ADDR), .we(DBUS_WRITE), .oe(DBUS_READ), .clk(CLK), .din(DBUS_IDATA_L), .dout(ram_1_dout));
  RAM #(.addrWidth(15), .dataWidth(24), .databus("bibus")) ram_2 (
    .addr(DBUS_ADDR), .we(DBUS_WRITE), .oe(DBUS_READ), .clk(CLK), .din(DBUS_IDATA_H), .dout(ram_2_dout));
  Comparator #(.width(15)) comparator_1 (.a(DBUS_ADDR), .b({15{1'b0}}), .eq(comparator_1_eq));  // open: gt, lt
  Comparator #(.width(15)) comparator_2 (.a(DBUS_ADDR), .b({15{1'b0}}), .eq(comparator_2_eq));  // open: gt, lt
  Multiplexer #(.width(24), .enable("false")) multiplexer_1 (
    .in0(ram_1_dout), .in1({24{1'b0}}), .out(multiplexer_1_out), .sel(comparator_1_eq));
  Multiplexer #(.width(24), .enable("false")) multiplexer_2 (
    .in0(ram_2_dout), .in1({24{1'b0}}), .out(multiplexer_2_out), .sel(comparator_2_eq));
  Register #(.width(24)) register_1 (.D(multiplexer_1_out), .en(DBUS_READ), .clk(CLK), .Q(DBUS_ODATA_L), .clr(1'b0));
  Register #(.width(1)) register_2 (.D(or_1_out), .en(1'b1), .clk(CLK), .Q(DBUS_DONE), .clr(1'b0));
  or or_1 (or_1_out, DBUS_WRITE, DBUS_READ);
  Register #(.width(24)) register_3 (.D(multiplexer_2_out), .en(DBUS_READ), .clk(CLK), .Q(DBUS_ODATA_H), .clr(1'b0));
endmodule

module JMP_TBL (
  input  [23:0] CMD,
  output [8:0] MC_ADDR
);

  wire [8:0] rom_1_data, rom_2_data;

  ROM #(.addrWidth(6), .dataWidth(9)) rom_1 (.addr(CMD[17:12]), .data(rom_1_data));
  ROM #(.addrWidth(4), .dataWidth(9)) rom_2 (.addr(CMD[18:15]), .data(rom_2_data));
  Multiplexer #(.width(9), .enable("false")) multiplexer_1 (
    .in0(rom_1_data), .in1(rom_2_data), .out(MC_ADDR), .sel(CMD[19]));

  // Notes on the sheet:
  //   contents of rom_1 (hex, n*v repeats v):
  //   19 1b 1f 20 24 25 26 27 28 2a 2d 30 33 34 37 38 39 3a 3b 3c 3d 3e 3f 42 43 44 46 47 48 49 4a 4c 4d
  //   4e 52 53 55 56 57 58 59 5a 5b 5c 5d 5e 5f 60 61 62 63 64 65 66 67 68 69 6a 6b 6c 6d 6e 6f 70
  //   contents of rom_2 (hex, n*v repeats v):
  //   71 72 73 75 77 78 79 7d 81 83 85 86 87 8b 8f 90
endmodule

module MC_ROM (
  input  [8:0] ADDR,
  output [31:0] UOP_L,
  output [31:0] UOP_H
);

  ROM #(.addrWidth(9), .dataWidth(32)) MC_L (.addr(ADDR), .data(UOP_L));
  ROM #(.addrWidth(9), .dataWidth(32)) MC_H (.addr(ADDR), .data(UOP_H));

  // Notes on the sheet:
  //   contents of MC_L (hex, n*v repeats v):
  //   a40000 1010000 a40001 a40002 a40003 a40004 a40005 a40006 a40007 a40008 a40009 a4000a a4000b a4000c
  //   a4000d a4000e a4000f 18000001 4*0 12 0 12 0 12 0 1b0000f 4100800f 12 12 4100000f 1ac000f 8000 5*12
  //   8000 12 8000 200 12 8000 600 12 8000 a00 12 12 8000 400 9*12 8000 800 12 12 12 20000 5*12 800 12 12
  //   e40012 e40000 1b0000f 4100800f 12 3010012 41ac000f 3010012 c80012 82d80012 28*12 0 14 0 14 940012
  //   980012 7b 12 0 12 7f 12 0 12 0 12 8800000 12 12 12 89 12 8000000 12 400008d 12 8000000 12 12 4000092
  //   12 88c0000 12
  //   contents of MC_H (hex, n*v repeats v):
  //   0 80 15*0 18000 c 10 c 2010 12 4000 12 40 12 40 0 a0 12 12 40 0 a0 5*12 a0 12 20 40080 12 20 40080
  //   12 20 40080 12 12 20 40080 9*12 20 40080 12 12 12 80 5*12 80 12 12 12 0 0 a0 12 92 40 92 30*12 100
  //   2012 121 2012 12 12 800 12 10000 12 200 12 10000 12 10000 12 10000 12 12 12 20000 12 10000 12 0 12
  //   10000 12 12 0 12 10000 12
endmodule

module REG_48 (
  input  CLK,
  input  WE,
  input  [23:0] D_L,
  input  [23:0] D_H,
  output [23:0] Q_L,
  output [23:0] Q_H
);

  Register #(.width(24)) register_1 (.D(D_L), .en(WE), .clk(CLK), .Q(Q_L), .clr(1'b0));
  Register #(.width(24)) register_2 (.D(D_H), .en(WE), .clk(CLK), .Q(Q_H), .clr(1'b0));
endmodule

module OP_SPLITTER (
  input  [23:0] OPCODE,
  output OP_LFLAG,
  output [3:0] OP_IR,
  output [3:0] OP_LCMD,
  output [5:0] OP_SCMD,
  output [14:0] OP_ADDR
);

  wire [2:0] bit_extender_2_out;
  wire [14:0] bit_extender_1_out;

  Bit_Extender #(.in_width(24), .out_width(15), .\type ("zero")) bit_extender_1 (.in(OPCODE), .out(bit_extender_1_out));
  assign bit_extender_2_out = {{2{OPCODE[18]}}, OPCODE[18]};  // Bit_Extender bit_extender_2
  Multiplexer #(.width(15), .enable("false")) multiplexer_1 (
    .in0({bit_extender_2_out, OPCODE[11:0]}), .in1(bit_extender_1_out), .out(OP_ADDR), .sel(OPCODE[19]));

  assign OP_IR = OPCODE[23:20];
  assign OP_LCMD = OPCODE[18:15];
  assign OP_LFLAG = OPCODE[19];
  assign OP_SCMD = OPCODE[17:12];
endmodule

module PC_NEXT (
  input  [2:0] P_SEL_PC,
  output [15:0] PC_NEXT
);

  wire [8:0] imm;
  wire [14:0] bit_extender_1_out, Mi, Uaddr, Vaddr;
  wire [15:0] adder_1_out, PC_Q;

  assign bit_extender_1_out = {{6{imm[8]}}, imm};  // Bit_Extender bit_extender_1
  Adder #(.width(16)) adder_1 (.a(PC_Q), .b(16'h1), .out(adder_1_out));  // open: cin, cout
  Multiplexer #(.select(3), .width(16), .enable("false")) multiplexer_1 (
    .in0({bit_extender_1_out, 1'b0}), .in1({Mi, 1'b0}), .in2(adder_1_out), .in3({Vaddr, 1'b0}),
    .in4({Uaddr, 1'b0}), .sel(P_SEL_PC));  // open: in5, in6, in7, out
  // AND_Gate and_1 is placed but not wired
  Multiplexer #(.width(16), .enable("false")) multiplexer_2 (
    .in0(PC_Q), .in1(adder_1_out), .out(PC_NEXT));  // open: sel
endmodule

module CYC_CNT (
  input  CLK,
  input  EN,
  output [29:0] CNT
);

  Counter #(.width(30), .max('h3fffffff)) counter_1 (
    .up(1'b1), .count(EN), .clk(CLK), .Q(CNT));  // open: clr, load, D, carry
endmodule
